# Fritzing sketch CO2 sensor on Pi Pico (saved by Fritzing 0.9.3b)

parts:
  Mod1 = Raspberry Pi Pico
  TD-er1 = MH-Z19 CO2 sensor [part_number=MH-Z19]
  OLED1 = OLED 1.3" 128x64 I2C SSH1106 (GND/VCC)

nets:
  N1: Mod1.pin_6, TD-er1.RX
  N2: Mod1.pin_7, TD-er1.TX
  N3: Mod1.pin_21, OLED1.SDA
  N4: Mod1.pin_22, OLED1.SCL
  GND: Mod1.pin_23, Mod1.pin_38, Mod1.pin_42, TD-er1.GND, OLED1.GND
  N5: Mod1.pin_24, OLED1.VCC
  N6: Mod1.pin_40, TD-er1.Vin

custom parts:
  Raspberry Pi Pico: Raspberry Pi Pico. Based around the RP2040 microcontroller the Pico is a low cost microcontroller device bringing Raspberry Pi quality, cost, and easy of use to the microcontroller space. Jan 2021, Split part in to two versions: tht (this one) and SMD. This one will drill holes for a .1 in header in pcb to allow plugging in the module as well as providing pads to solder the module to the top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
  OLED 1.3" 128x64 I2C SSH1106 (GND/VCC): OLED 1.3" 128x64 I2C SSH1106 Pinout: GND/VCC/SCL/SDA
